# Fritzing sketch led-flash (saved by Fritzing 0.9.3b)

parts:
  Raspberry_Pi_2 = Raspberry Pi 3 [part_number=RPI-3-V1.2]
  D1 = LTE-302 [package=lte-302]

nets:
  N1: Raspberry_Pi_2.GPIO2, D1.A
  N2: Raspberry_Pi_2.5V, D1.C

notes:
  Engine
